// Logisim project lab 2.circ as structural Verilog: 1 circuit, main circuit main
module main (
  input  [1:0] in_1,
  input  [1:0] in_2,
  input  in_3,
  input  in_4,
  input  in_5,
  input  in_6,
  input  [1:0] in_7,
  input  in_8,
  input  in_9,
  input  in_10,
  input  [1:0] in_11,
  input  in_12,
  input  [1:0] in_13,
  input  in_14,
  input  [1:0] in_15,
  input  in_16,
  input  in_17,
  input  [1:0] in_18,
  input  [1:0] in_19,
  input  in_20,
  input  in_21,
  input  in_22,
  input  [7:0] in_23,
  input  in_24,
  input  in_25,
  input  in_26,
  input  in_27,
  input  in_28,
  input  in_29,
  input  in_30,
  input  in_31,
  input  in_32,
  input  in_33,
  input  in_34,
  input  in_35,
  output [1:0] out_36,
  output out_37,
  output out_38,
  output out_39,
  output out_40,
  output [1:0] out_41,
  output out_42,
  output out_43,
  output out_44,
  output [1:0] out_45,
  output out_46,
  output [7:0] out_47,
  output [7:0] out_48,
  output out_49,
  output [7:0] out_50,
  output out_51
);

  wire and_2_out, and_3_out, and_4_out, and_7_out, and_8_out, and_9_out, and_10_out, not_1_out, not_4_out,
       xor_2_out;
  wire [1:0] and_5_out, and_6_out, not_2_out, not_3_out;

  nand nand_1 (out_38, in_9, in_9, in_10);
  assign out_41 = in_11 & in_11 & in_13;  // AND_Gate and_1, 2 bits wide
  or or_1 (out_44, in_16, in_16, in_17, in_17);
  assign out_45 = in_18 ^ in_19;  // XOR_Gate xor_1, 2 bits wide
  xor xor_2 (xor_2_out, in_20, in_21);
  and and_2 (and_2_out, in_20, in_21);
  and and_3 (and_3_out, in_20, in_22);
  and and_4 (and_4_out, in_21, in_22);
  not not_1 (not_1_out, in_28);
  assign not_2_out = ~in_1;  // NOT_Gate not_2, 2 bits wide
  assign not_3_out = ~in_2;  // NOT_Gate not_3, 2 bits wide
  xor xor_3 (out_46, xor_2_out, in_22);
  assign and_5_out = not_2_out & in_2;  // AND_Gate and_5, 2 bits wide
  assign and_6_out = in_1 & not_3_out;  // AND_Gate and_6, 2 bits wide
  or or_2 (out_49, and_2_out, and_3_out, and_4_out);
  not not_4 (not_4_out, in_29);
  and and_7 (and_7_out, in_32, not_4_out, not_1_out);
  and and_8 (and_8_out, in_33, not_1_out, in_29);
  and and_9 (and_9_out, in_34, in_28, not_4_out);
  and and_10 (and_10_out, in_35, in_28, in_29);
  assign out_36 = and_5_out | and_5_out | and_6_out | and_6_out;  // OR_Gate or_3, 2 bits wide
  or or_4 (out_51, and_7_out, and_8_out, and_9_out, and_10_out);
  Demultiplexer #(.select(2)) demultiplexer_1 (
    .out0(out_39), .out1(out_40), .out2(out_42), .out3(out_43), .in(in_12), .sel(in_15), .en(in_14));
  RAM ram_1 (.addr(in_23), .data(out_47), .sel(in_24), .ld(in_25), .clr(in_26));  // open: clk
  Multiplexer #(.select(2)) multiplexer_1 (
    .in0(in_3), .in1(in_4), .in2(in_5), .in3(in_6), .out(out_37), .sel(in_7), .en(in_8));
  Multiplexer #(.width(8)) multiplexer_2 (.in0(out_47), .in1(out_48), .out(out_50), .sel(in_30), .en(in_31));
  ROM rom_1 (.addr(in_23), .data(out_48), .sel(in_27));

  // Notes on the sheet:
  //   Task 1
  //   Task 2
  //   Task 3
  //   Task 4
  //   Task 5
  //   contents of rom_1 (hex, n*v repeats v):
  //   aa 0 a 0 0 ff 7*0 a2
endmodule
